# Fritzing sketch Schaltplan (saved by Fritzing 0.9.2b)

parts:
  2 = Arduino Uno (Rev3)
  3 = Raspberry Pi 2  # not connected
  1 = Power plug  # not connected
  M1 = DC Motor  # not connected
  M2 = DC Motor  # not connected
  5 = Peltier Element  # not connected
  J1 = Infrared Proximity Sensor

nets:
  N1: 2.D0/RX, J1.Vout
